# Fritzing sketch arduino-piezos (saved by Fritzing 0.9.3b)
circuit board: 9.4cm x 4.8cm
breadboards: 1

parts:
  R0 = Resistor [tolerance=±5% resistance=1M package=THT]
  R1 = Resistor [tolerance=±5% resistance=1M package=THT]
  D1 = Zener Diode 2 [part_number=1N4732A package="300 mil [THT]"]
  D0 = Zener Diode 2 [part_number=1N4732A package="300 mil [THT]"]
  R2 = Resistor [tolerance=±5% resistance=1M package=THT]
  R3 = Resistor [tolerance=±5% resistance=1M package=THT]
  D2 = Zener Diode 2 [part_number=1N4732A package="300 mil [THT]"]
  D3 = Zener Diode 2 [part_number=1N4732A package="300 mil [THT]"]
  U1 = 6.35mm Mono Audio Jack [package=audio-jack]
  U2 = 6.35mm Mono Audio Jack [package=audio-jack]
  U3 = 6.35mm Mono Audio Jack [package=audio-jack]
  U4 = 6.35mm Mono Audio Jack [package=audio-jack]
  J4 = Screw terminal - 5 pins - 3.5mm pin spacing [package=THT]

nets:
  N1: R0.Pin_0, R1.Pin_0, D1.anode, D0.anode, R2.Pin_0, R3.Pin_0, D2.anode, D3.anode, U1.SLEEVE, U2.SLEEVE, U3.SLEEVE, U4.SLEEVE, J4.pin1
  N2: R0.Pin_1, D0.cathode, U1.SIGNAL, J4.pin2
  N3: R1.Pin_1, D1.cathode, U2.SIGNAL, J4.pin3
  N4: R2.Pin_1, D2.cathode, U3.SIGNAL, J4.pin4
  N5: R3.Pin_1, D3.cathode, U4.SIGNAL, J4.pin5

notes:
  Gnd, A0, A1, A2, A3
  GND
  A0
  A1
  A2
  A3
  Piezo to
  Arduino
  Fire Ancestor

custom parts:
  Zener Diode 2: A standard zener diode with corrected terminal points (YL)
  6.35mm Mono Audio Jack: 6.35mm MONO PCB mount audio jack.
  Screw terminal - 5 pins - 3.5mm pin spacing: Screw terminal with 5 pins. 3.5mm pin spacing
